// Digital circuit decoder.dig as structural Verilog
module decoder (
  input  [15:0] RL,
  input  [15:0] RR,
  input  [31:0] instr,
  output [1:0] rs,
  output [1:0] rd,
  output add,
  output [15:0] L,
  output [15:0] R,
  output jump
);

  Multiplexer #(.Bits(16)) multiplexer_1 (.sel(instr[27]), .in_0(instr[15:0]), .in_1(RR), .out(R));
  Multiplexer #(.Bits(16)) multiplexer_2 (.sel(instr[27]), .in_0(RR), .in_1(RL), .out(L));
  Decoder #(.Selector_Bits(3)) decoder_1 (
    .sel(instr[26:24]), .out_0(add), .out_7(jump));  // open: out_1, out_2, out_3, out_4, out_5, out_6

  assign rd = instr[17:16];
  assign rs = instr[21:20];
endmodule
