// Digital circuit execute.dig as structural Verilog
module execute (
  input  [15:0] L,
  input  [15:0] R,
  input  [2:0] op,
  output [15:0] result,
  output halt,
  output error
);

  wire musteq, musteq_eq, not_1_out;
  wire [15:0] add_1_s;

  Decoder #(.Selector_Bits(3)) decoder_1 (
    .sel(op), .out_5(musteq));  // open: out_0, out_1, out_2, out_3, out_4, out_6, out_7
  Add #(.Bits(16)) add_1 (.a(L), .b(R), .c_i(1'b0), .s(add_1_s));  // open: c_o
  Comparator #(.Bits(16)) u_musteq (.a(R), .b(L), .eq(musteq_eq));  // open: gt, lt
  not not_1 (not_1_out, musteq_eq);
  and and_1 (halt, musteq_eq, musteq);
  and and_2 (error, musteq, not_1_out);
  Multiplexer #(.Selector_Bits(3), .Bits(16)) multiplexer_1 (
    .sel(op), .in_0(add_1_s), .in_1({16{1'b0}}), .in_2({16{1'b0}}), .in_3({16{1'b0}}), .in_4({16{1'b0}}),
    .in_5(L), .in_6(R), .in_7(L), .out(result));
endmodule
