// Digital circuit frontpanel.dig as structural Verilog
module frontpanel (
  input  clock,
  input  erun,
  input  DC,
  output [15:0] R0,
  output [15:0] R1,
  output [15:0] R2,
  output [15:0] R3,
  output [7:0] PC,
  output halt,
  output error
);

  wire aluopdisplay_1_p1, aluopdisplay_1_p2, cond, hex, hexdisplay_1_p2, hexdisplay_1_p5, hexdisplay_1_p8,
       hexdisplay_1_p10, hexdisplay_1_p13, hexdisplay_2_p2, hexdisplay_2_p5, hexdisplay_2_p8,
       hexdisplay_2_p10, hexdisplay_2_p13, hexdisplay_3_p2, hexdisplay_3_p5, hexdisplay_3_p8,
       hexdisplay_3_p11, hexdisplay_3_p13, hexdisplay_3_p17, hexdisplay_3_p18, hexdisplay_3_p21,
       hexdisplay_3_p23, hexdisplay_3_p26, imm, immv, instrdisplay_1_p2, instrdisplay_1_p4,
       instrdisplay_1_p7, instrdisplay_1_p9, instrdisplay_1_p12, instrdisplay_1_p14, jump, L, L_valid, MC,
       op, R, R_valid, rd_valid, regdisplay_1_p1, regdisplay_1_p2, regdisplay_2_p1, regdisplay_2_p2,
       regdisplay_3_p1, regdisplay_3_p2, res_valid, result, rj32_1_p4, rs_valid, run_t, skip, slow_t,
       stalled_t, step_t, vga_frontpanel_1_p21;
  wire [2:0] aluop;
  wire [3:0] hexdisplay_1_p1, hexdisplay_1_p4, hexdisplay_1_p6, hexdisplay_1_p9, hexdisplay_1_p12,
       hexdisplay_2_p1, hexdisplay_2_p4, hexdisplay_2_p6, hexdisplay_2_p9, hexdisplay_2_p12, hexdisplay_3_p1,
       hexdisplay_3_p4, hexdisplay_3_p6, hexdisplay_3_p9, hexdisplay_3_p10, hexdisplay_3_p15,
       hexdisplay_3_p16, hexdisplay_3_p19, hexdisplay_3_p22, hexdisplay_3_p25, rd, rs;
  wire [7:0] rj32_1_p2;
  wire [13:0] rj32_1_p6;
  wire [15:0] aluopdisplay_1_d1, aluopdisplay_1_d2, Data_d, instrdisplay_1_p1, instrdisplay_1_p3,
       instrdisplay_1_p6, instrdisplay_1_p8, instrdisplay_1_p10, instrdisplay_1_p13, Program_d,
       regdisplay_1_d1, regdisplay_1_d2, regdisplay_2_d1, regdisplay_2_d2, regdisplay_3_d1, regdisplay_3_d2,
       rj32_1_p5;

  BlockRAMDualPort #(.AddrBits(8), .isProgramMemory("true"), .Bits(16)) Program (
    .A(rj32_1_p2), .Din({16{1'b0}}), .str(1'b0), .C(MC), .D(Program_d));
  BlockRAMDualPort #(.AddrBits(14), .Bits(16)) Data (
    .A(rj32_1_p6), .Din(rj32_1_p5), .str(rj32_1_p4), .C(MC), .D(Data_d));
  Button step (.out(step_t));
  Button slow (.out(slow_t));
  Button run (.out(run_t));
  LED stalled (.in(stalled_t));
  SixteenSeg sixteenseg_1 (.led(regdisplay_1_d1), .dp(regdisplay_1_p1));
  SixteenSeg sixteenseg_2 (.led(regdisplay_1_d2), .dp(regdisplay_1_p2));
  regdisplay regdisplay_1 (
    .D1(regdisplay_1_d1), .P1(regdisplay_1_p1), .D2(regdisplay_1_d2), .P2(regdisplay_1_p2), .R(rd), .J(jump),
    .E(res_valid));
  // rj32 rj32_1: pin names not known; wires that end beside it: MC, rj32_1_p2, Program_d, rj32_1_p4, rj32_1_p5, rj32_1_p6, Data_d, erun, jump, rd_valid, 1'b1, rs_valid, op, run_t, cond, L, slow_t, R, rd, step_t, rs, imm, clock, immv, aluop, stalled_t, PC, R0, R1, R2, R3, result, skip, halt, error
  SixteenSeg sixteenseg_3 (.led(instrdisplay_1_p1), .dp(instrdisplay_1_p2));
  SixteenSeg sixteenseg_4 (.led(instrdisplay_1_p3), .dp(instrdisplay_1_p4));
  // instrdisplay instrdisplay_1: pin names not known; wires that end beside it: instrdisplay_1_p1, instrdisplay_1_p2, instrdisplay_1_p3, instrdisplay_1_p4, op, instrdisplay_1_p6, instrdisplay_1_p7, instrdisplay_1_p8, instrdisplay_1_p9, instrdisplay_1_p10, cond, instrdisplay_1_p12, instrdisplay_1_p13, instrdisplay_1_p14
  Seven_Seg_Hex seven_seg_hex_1 (.d(hexdisplay_1_p1), .dp(hexdisplay_1_p2));
  Seven_Seg_Hex seven_seg_hex_2 (.d(hexdisplay_1_p4), .dp(hexdisplay_1_p5));
  // hexdisplay hexdisplay_1: pin names not known; wires that end beside it: hexdisplay_1_p1, hexdisplay_1_p2, res_valid, hexdisplay_1_p4, hexdisplay_1_p5, hexdisplay_1_p6, result, hexdisplay_1_p8, hexdisplay_1_p9, hexdisplay_1_p10, hex, hexdisplay_1_p12, hexdisplay_1_p13
  SixteenSeg sixteenseg_5 (.led(instrdisplay_1_p6), .dp(instrdisplay_1_p7));
  SixteenSeg sixteenseg_6 (.led(instrdisplay_1_p8), .dp(instrdisplay_1_p9));
  Seven_Seg_Hex seven_seg_hex_3 (.d(hexdisplay_1_p6), .dp(hexdisplay_1_p8));
  Seven_Seg_Hex seven_seg_hex_4 (.d(hexdisplay_1_p9), .dp(hexdisplay_1_p10));
  SixteenSeg sixteenseg_7 (.led(instrdisplay_1_p10), .dp(instrdisplay_1_p12));
  SixteenSeg sixteenseg_8 (.led(instrdisplay_1_p13), .dp(instrdisplay_1_p14));
  Seven_Seg_Hex seven_seg_hex_5 (.d(hexdisplay_1_p12), .dp(hexdisplay_1_p13));
  SixteenSeg sixteenseg_9 (.led(regdisplay_2_d1), .dp(regdisplay_2_p1));
  regdisplay regdisplay_2 (
    .D1(regdisplay_2_d1), .P1(regdisplay_2_p1), .D2(regdisplay_2_d2), .P2(regdisplay_2_p2), .R(rd), .J(jump),
    .E(1'b1));
  Seven_Seg_Hex seven_seg_hex_6 (.d(hexdisplay_2_p1), .dp(hexdisplay_2_p2));
  Seven_Seg_Hex seven_seg_hex_7 (.d(hexdisplay_2_p4), .dp(hexdisplay_2_p5));
  // hexdisplay hexdisplay_2: pin names not known; wires that end beside it: hexdisplay_2_p1, hexdisplay_2_p2, L_valid, hexdisplay_2_p4, hexdisplay_2_p5, hexdisplay_2_p6, L, hexdisplay_2_p8, hexdisplay_2_p9, hexdisplay_2_p10, hex, hexdisplay_2_p12, hexdisplay_2_p13
  SixteenSeg sixteenseg_10 (.led(regdisplay_2_d2), .dp(regdisplay_2_p2));
  Seven_Seg_Hex seven_seg_hex_8 (.d(hexdisplay_2_p6), .dp(hexdisplay_2_p8));
  Seven_Seg_Hex seven_seg_hex_9 (.d(hexdisplay_2_p9), .dp(hexdisplay_2_p10));
  SixteenSeg sixteenseg_11 (.led(regdisplay_3_d1), .dp(regdisplay_3_p1));
  SixteenSeg sixteenseg_12 (.led(regdisplay_3_d2), .dp(regdisplay_3_p2));
  DipSwitch u_hex (.out(hex));
  regdisplay regdisplay_3 (
    .D1(regdisplay_3_d1), .P1(regdisplay_3_p1), .D2(regdisplay_3_d2), .P2(regdisplay_3_p2), .R(rs), .J(1'b0),
    .E(rs_valid));
  Seven_Seg_Hex seven_seg_hex_10 (.d(hexdisplay_2_p12), .dp(hexdisplay_2_p13));
  // vga_frontpanel vga_frontpanel_1: pin names not known; wires that end beside it: PC, R0, R1, R2, R3, L, R, imm, immv, op, clock, cond, rd, rd_valid, rs, DC, rs_valid, result, jump, skip, vga_frontpanel_1_p21, aluop, halt, error
  Seven_Seg_Hex seven_seg_hex_11 (.d(hexdisplay_3_p1), .dp(hexdisplay_3_p2));
  // hexdisplay hexdisplay_3: pin names not known; wires that end beside it: hexdisplay_3_p1, hexdisplay_3_p2, immv, hexdisplay_3_p4, hexdisplay_3_p5, hexdisplay_3_p6, imm, hexdisplay_3_p8, hexdisplay_3_p9, hexdisplay_3_p10, hexdisplay_3_p11, R_valid, hexdisplay_3_p13, hex, hexdisplay_3_p15, hexdisplay_3_p16, hexdisplay_3_p17, hexdisplay_3_p18, hexdisplay_3_p19, R, hexdisplay_3_p21, hexdisplay_3_p22, hexdisplay_3_p23, hex, hexdisplay_3_p25, hexdisplay_3_p26
  SixteenSeg sixteenseg_13 (.led(aluopdisplay_1_d1), .dp(aluopdisplay_1_p1));
  SixteenSeg sixteenseg_14 (.led(aluopdisplay_1_d2), .dp(aluopdisplay_1_p2));
  aluopdisplay aluopdisplay_1 (
    .D1(aluopdisplay_1_d1), .P1(aluopdisplay_1_p1), .D2(aluopdisplay_1_d2), .P2(aluopdisplay_1_p2),
    .I(aluop), .Q(res_valid), .R(R_valid), .L(L_valid));
  Seven_Seg_Hex seven_seg_hex_12 (.d(hexdisplay_3_p4), .dp(hexdisplay_3_p5));
  Seven_Seg_Hex seven_seg_hex_13 (.d(hexdisplay_3_p6), .dp(hexdisplay_3_p8));
  Seven_Seg_Hex seven_seg_hex_14 (.d(hexdisplay_3_p9), .dp(hexdisplay_3_p11));
  Seven_Seg_Hex seven_seg_hex_15 (.d(hexdisplay_3_p10), .dp(hexdisplay_3_p13));
  Seven_Seg_Hex seven_seg_hex_16 (.d(hexdisplay_3_p16), .dp(hexdisplay_3_p18));
  Seven_Seg_Hex seven_seg_hex_17 (.d(hexdisplay_3_p15), .dp(hexdisplay_3_p17));
  Seven_Seg_Hex seven_seg_hex_18 (.d(hexdisplay_3_p19), .dp(hexdisplay_3_p21));
  hexdisplay hexdisplay_4 ();  // open: E, V, D1, P1, D2, P2, D3, P3, D4, P4, D5, P5, D6, P6, D7, P7, D8, P8
  DipSwitch dipswitch_1 (.out(vga_frontpanel_1_p21));
  Seven_Seg_Hex seven_seg_hex_19 (.d(hexdisplay_3_p22), .dp(hexdisplay_3_p23));
  Seven_Seg_Hex seven_seg_hex_20 (.d(hexdisplay_3_p25), .dp(hexdisplay_3_p26));
  LED u_skip (.in(skip));

  // Other names for the same wires on the sheet: C = clock

  // Notes on the sheet:
  //   clock: Hz: 10
  //   DC: Hz: 2147483647
  //   rj45 Creates
  //   =
endmodule
