// Digital circuit testsuite.dig as structural Verilog
module testsuite (
  input  clock,
  output error,
  output halt,
  output [3:0] PC
);

  frontpanel frontpanel_1 (.clock(clock), .PC(PC), .halt(halt), .error(error));  // open: R0, R1, R2, R3
endmodule

/* Test case add:
clock error halt

# #include "../cpudef.asm"
# 
# move r1, 5
# move r2, 3
# add r1, r2
# add r1, 2
# eq r1, 10
# halt

program(0x2b0b, 0x1b13, 0x810a, 0x100b, 0x520b, 0x0008)

let i = 0;
while(!(halt | error | (i >= 100)))
  let i = i + 1;
  0 0 0
  1 x x
end while
0 0 1
*/

/* Test case jump:
clock error halt

# #include "../cpudef.asm"
# 
#   jump one
# three:
#   add r0, r1
#   add r0, r2
#   jump end
# two:
#   move r2, 2
#   jump three
# one:
#   move r1, 3
#   jump two
# end:
#   eq r0, 5
#   halt

program(0x00c1, 0x8082, 0x8102, 0x0101, 0x1313, 0x0021, 0x1b0b, 0x0081, 0x2a03, 0x0008)

let i = 0;
while(!(halt | error | (i >= 100)))
  let i = i + 1;
  0 0 0
  1 x x
end while
0 0 1
*/

/* Test case conditionals:
clock error halt

# #include "../cpudef.asm"
# 
#   brt end
#   brf one
# three:
#   add r0, r1
#   add r0, r2
#   eq r2, 5
#   brt one
#   jump end
# two:
#   move r2, 2
#   eq r1, 5
#   brf three
# one:
#   move r1, 3
#   eq r1, 3
#   brt two
# end:
#   eq r0, 5
#   halt

program(0x01b1, 0x0159, 0x8082, 0x8102, 0x2a13, 0x0151, 0x01a1, 0x1313, 0x2a0b, 0x0059, 0x1b0b, 0x1a0b, 0x00f1, 0x2a03, 0x0008)

let i = 0;
while(!(halt | error | (i >= 100)))
  let i = i + 1;
  0 0 0
  1 x x
end while
0 0 1
*/
