// Digital circuit vga_blinkenlights.dig as structural Verilog
module vga_blinkenlights (
  input  clock,
  input  [25:0] db,
  input  [11:0] res_H,
  input  [11:0] fp_H,
  input  [11:0] sync_H,
  input  [11:0] bp_H,
  input  neg_H,
  input  [11:0] res_V,
  input  [11:0] fp_V,
  input  [11:0] sync_V,
  input  [11:0] bp_V,
  input  neg_V,
  input  [15:0] TD,
  input  [7:0] MD,
  input  [7:0] fbr_D,
  input  [3:0] fbc_D,
  output [3:0] R,
  output [3:0] G,
  output [3:0] B,
  output hs,
  output vs,
  output de,
  output [10:0] TA,
  output [9:0] MA,
  output wen,
  output [8:0] fbw_A,
  output [7:0] fbw_D,
  output [8:0] fbr_A
);

  wire vb;
  wire [4:0] sub_1_s, vga_debugrender_1_db_a;
  wire [5:5] sub_1_s_2;
  wire [7:0] X;
  wire [7:4] Y;
  wire [15:0] debugcopy_1_db_d;

  Sub #(.Bits(6)) sub_1 (.a(X[5:0]), .b(6'b000100), .c_i(1'b0), .s({sub_1_s_2[5], sub_1_s}));  // open: c_o
  debugcopy debugcopy_1 (
    .db(db), .clock(clock), .e(vb), .db_A(vga_debugrender_1_db_a), .db_D(debugcopy_1_db_d));  // open: decode, ctrl
  Multiplexer #(.Bits(5)) multiplexer_1 (.sel(sub_1_s_2[5]), .in_0(sub_1_s), .in_1({5{1'b0}}), .out(fbr_A[4:0]));
  vga_debugrender vga_debugrender_1 (
    .db_D(debugcopy_1_db_d), .clock(clock), .\signed (1'b1), .hex(1'b0), .fb_A(fbw_A), .fb_D(fbw_D[6:0]),
    .fb_wen(wen), .db_A(vga_debugrender_1_db_a));  // open: colour
  vga_display vga_display_1 (
    .clock(clock), .res_H(res_H), .fp_H(fp_H), .sync_H(sync_H), .bp_H(bp_H), .neg_H(neg_H), .res_V(res_V),
    .fp_V(fp_V), .sync_V(sync_V), .bp_V(bp_V), .neg_V(neg_V), .char(fbr_D[6:0]), .fg(fbc_D), .bg({12{1'b0}}),
    .TD(TD), .MD(MD), .R(R), .G(G), .B(B), .hs(hs), .vs(vs), .de(de), .CX(X), .CY({Y, fbr_A[8:5]}),
    .vblank(vb), .TA(TA), .MA(MA));  // open: hblank

  assign fbw_D[7] = 1'b0;

  // Other names for the same wires on the sheet: C = clock; Y[3:0] = fbr_A[8:5]

  // Notes on the sheet:
  //   clock: Hz: 5
  //   res_H: default 640
  //   fp_H: default 16
  //   sync_H: default 96
  //   bp_H: default 48
  //   res_V: default 400
  //   fp_V: default 12
  //   sync_V: default 2
  //   bp_V: default 35
endmodule
